// Digital circuit ALU_generica.dig as structural Verilog
module ALU_generica (
  input  [31:0] A,
  input  [31:0] B,
  input  [2:0] ALUOp,
  output alu_out,
  output zero
);

  SomadorVetorialLimpo somadorvetoriallimpo_1 ();  // open: mode_i, vecSize, A, B, lookAhead_out, sum_out
  LeftShifter leftshifter_1 ();  // open: data_in, shift_in, data_out
  RightShifter rightshifter_1 ();  // open: data_in, shift_in, out
endmodule
