// Digital circuit ImmGen.dig as structural Verilog
module ImmGen (
  input  [31:0] instruction
);

  wire instruct_comparator_1_p3, instruct_comparator_2_p3, instruct_comparator_3_p3,
       instruct_comparator_4_p3, instruct_comparator_5_p3, instruct_comparator_6_p3,
       instruct_comparator_7_p3, instruct_comparator_8_p3, or_1_out, or_2_out;
  wire [2:0] priorityencoder_1_num;

  // NotConnected on instruction[7]
  // instruct_comparator instruct_comparator_1: pin names not known; wires that end beside it: instruction[6:0], 7'b0000011, instruct_comparator_1_p3
  // instruct_comparator instruct_comparator_2: pin names not known; wires that end beside it: instruction[6:0], 7'b0010011, instruct_comparator_2_p3
  // instruct_comparator instruct_comparator_3: pin names not known; wires that end beside it: instruction[6:0], 7'b1100111, instruct_comparator_3_p3
  // instruct_comparator instruct_comparator_4: pin names not known; wires that end beside it: instruction[6:0], 7'b0100011, instruct_comparator_4_p3
  // instruct_comparator instruct_comparator_5: pin names not known; wires that end beside it: instruction[6:0], 7'b1100011, instruct_comparator_5_p3
  // instruct_comparator instruct_comparator_6: pin names not known; wires that end beside it: instruction[6:0], 7'b0110111, instruct_comparator_6_p3
  // instruct_comparator instruct_comparator_7: pin names not known; wires that end beside it: instruction[6:0], 7'b0010111, instruct_comparator_7_p3
  // instruct_comparator instruct_comparator_8: pin names not known; wires that end beside it: instruction[6:0], 7'b1101111, instruct_comparator_8_p3
  or or_1 (or_1_out, instruct_comparator_1_p3, instruct_comparator_2_p3, instruct_comparator_3_p3);
  or or_2 (or_2_out, instruct_comparator_6_p3, instruct_comparator_7_p3);
  PriorityEncoder #(.Selector_Bits(3)) priorityencoder_1 (
    .in0(or_1_out), .in1(instruct_comparator_4_p3), .in2(instruct_comparator_5_p3), .in3(or_2_out),
    .in4(instruct_comparator_8_p3), .in5(1'b0), .in6(1'b0), .in7(1'b0), .num(priorityencoder_1_num));  // open: any
  // Pins of 1 and 25 bits meet at instruction[31:7]

  // Notes on the sheet:
  //   I
  //   S
  //   SB
  //   UJ
  //   U
endmodule
