// Digital circuit cpu.dig as structural Verilog
module cpu (
);

  BancoRegistradores bancoregistradores_1 ();  // open: rs_2, rd, rs_1, WriteData, Clock, regWrite, readData1, readData2
  LeftShifter leftshifter_1 ();  // open: data_in, shift_in, data_out
  RightShifter rightshifter_1 ();  // open: data_in, shift_in, data_out
endmodule
